# Fritzing sketch fritzing (saved by Fritzing 0.9.5d)
breadboards: 1
perfboards: 1

parts:
  R2 = Resistor [tolerance=±1% resistance=2.2k package=THT]
  抵抗内蔵LED(5V) = smd LED [color="Red (633nm)" package="0603 [SMD]"]
  NchパワーMOSFET_60V5A_2SK4017 = Basic FET N-Channel [package="D2Pak [SMD]"]
  抵抗内蔵LED(5V)_2 = smd LED [color="Red (633nm)" package="0603 [SMD]"]
  R1 = Resistor [tolerance=±1% resistance=220k package=THT]
  Raspberry_Pi_Pico_WH = Raspberry Pi Pico H
  S1 = Pushbutton [package="[THT]"]
  NchパワーMOSFET_60V5A_2SK4017_2 = Basic FET N-Channel [package="D2Pak [SMD]"]
  R1_2 = Resistor [tolerance=±1% resistance=220k package=THT]
  R2_2 = Resistor [tolerance=±1% resistance=2.2k package=THT]
  パーツ2 = Arduino Nano Every
  Power_plug1 = Power plug
  M1 = Stepper Motor - Bipolar
  HC-SR04_Sensor_1 = HC-SR04 Ultrasonic Distance Sensor  # not connected
  HC-SR04_Sensor_2 = HC-SR04 Ultrasonic Distance Sensor  # not connected
  L298N2 = L298N DC motor driver
  LED1 = LED - 5mm [color="Red (633nm)" package="5 mm [THT]"]  # not connected
  R3 = Resistor [tolerance=±1% resistance=470 package=THT]  # not connected

nets:
  N1: R2.Pin_0, Raspberry_Pi_Pico_WH.GP17
  N2: R2.Pin_1, NchパワーMOSFET_60V5A_2SK4017.Gate, R1_2.Pin_0
  N3: 抵抗内蔵LED(5V).cathode, NchパワーMOSFET_60V5A_2SK4017_2.drain
  N4: 抵抗内蔵LED(5V).anode, 抵抗内蔵LED(5V)_2.anode, Raspberry_Pi_Pico_WH.VSYS, パーツ2.D11/MOSI, パーツ2.+5V, L298N2.5V#7
  N5: NchパワーMOSFET_60V5A_2SK4017.drain, 抵抗内蔵LED(5V)_2.cathode
  GND: NchパワーMOSFET_60V5A_2SK4017.source, R1.Pin_1, Raspberry_Pi_Pico_WH.GND, NchパワーMOSFET_60V5A_2SK4017_2.source, R1_2.Pin_1, パーツ2.GND, Power_plug1.GND, L298N2.GND
  N6: R1.Pin_0, NchパワーMOSFET_60V5A_2SK4017_2.Gate, R2_2.Pin_1
  N7: Raspberry_Pi_Pico_WH.3V3, S1.Pin_3, S1.Pin_4
  N8: Raspberry_Pi_Pico_WH.GP16, R2_2.Pin_0
  N9: Raspberry_Pi_Pico_WH.GP15, S1.Pin_1, S1.Pin_2
  N10: パーツ2.A3, L298N2.IN4
  N11: パーツ2.A2, L298N2.IN1
  N12: パーツ2.A1, L298N2.IN2
  N13: パーツ2.A0, L298N2.IN3
  VCC: Power_plug1.VCC, L298N2.12V
  N14: M1.A, L298N2.OUT2
  N15: M1.C, L298N2.OUT1
  N16: M1.B, L298N2.OUT4
  N17: M1.D, L298N2.OUT3
  N18: L298N2.5V#9, L298N2.ENA
  N19: L298N2.5V#10, L298N2.ENB

custom parts:
  Raspberry Pi Pico H: Raspberry Pi Pico H. Based around the RP2040 microcontroller the Pico H is a low cost microcontroller device bringing Raspberry Pi quality, cost, and easy of use to the microcontroller space.
  Arduino Nano Every: The Nano Every is Arduino’s 5V compatible board in the smallest available form factor: 45x18mm! The Arduino Nano is the preferred board for many projects requiring a small and easy to use microcontroller board. The small footprint and low price, make the Nano Every particularly suited for wearable inventions, low cost robotics, electronic musical instruments, and general use to control smaller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
  L298N DC motor driver: 2x DC motor driver with 78M05 positive voltage regulator (7..35 V) L298N: max 46 V, 2 A Set 5 V Enable jumper to enable 5 V regultor (needed for the L298N) and +5 V output at screw terminal or supply external +5 V at screw terminal Set ENA and/or ENB to +5 V to enable motor permanently or supply ENA and/or ENB with PWM signal IN1 and IN2 set rotation directory for motor A (OUT1/OUT2) IN2 and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
